// Logisim project Timelimited_tictactoc.circ as structural Verilog: 8 circuits, main circuit main
module main (
);

  wire and_1_out, and_2_out, GAME_START_p2, inputmemory_1_astate, inputmemory_1_p1_1, inputmemory_1_p1_2,
       inputmemory_1_p1_3, inputmemory_1_p1_4, inputmemory_1_p1_5, inputmemory_1_p1_6, inputmemory_1_p1_7,
       inputmemory_1_p1_8, inputmemory_1_p1_9, inputmemory_1_p2_1, inputmemory_1_p2_2, inputmemory_1_p2_3,
       inputmemory_1_p2_4, inputmemory_1_p2_5, inputmemory_1_p2_6, inputmemory_1_p2_7, inputmemory_1_p2_8,
       inputmemory_1_p2_9, n1_out, n2_out, n3_out, n4_out, n5_out, n6_out, n7_out, n8_out, n9_out, not_1_out,
       or_1_out, or_2_out, or_3_out, or_4_out, or_5_out, or_6_out, or_7_out, or_8_out, or_9_out, or_10_out,
       or_11_out, or_12_out, or_13_out, RESET_out, timer_1_b0, timer_1_b1, timer_1_b2, timer_1_t0,
       timer_1_t1, timer_1_t2, timer_1_t3, timer_1_timelimit, win_calc_1_win, win_calc_2_win;

  or or_1 (or_1_out, and_1_out, win_calc_2_win, win_calc_1_win);
  Inputmemory inputmemory_1 (
    .d_able(or_1_out), .k_9(n9_out), .k_8(n8_out), .k_7(n7_out), .k_6(n6_out), .k_5(n5_out), .k_4(n4_out),
    .k_3(n3_out), .k_2(n2_out), .k_1(n1_out), .reset(RESET_out), .TimeLimit(timer_1_timelimit),
    .p1_9(inputmemory_1_p1_9), .p1_8(inputmemory_1_p1_8), .p1_7(inputmemory_1_p1_7),
    .p1_6(inputmemory_1_p1_6), .p1_5(inputmemory_1_p1_5), .p1_4(inputmemory_1_p1_4),
    .p1_3(inputmemory_1_p1_3), .p1_2(inputmemory_1_p1_2), .p1_1(inputmemory_1_p1_1),
    .p2_9(inputmemory_1_p2_9), .p2_8(inputmemory_1_p2_8), .p2_7(inputmemory_1_p2_7),
    .p2_6(inputmemory_1_p2_6), .p2_5(inputmemory_1_p2_5), .p2_4(inputmemory_1_p2_4),
    .p2_3(inputmemory_1_p2_3), .p2_2(inputmemory_1_p2_2), .p2_1(inputmemory_1_p2_1),
    .Astate(inputmemory_1_astate));
  or or_2 (or_2_out, inputmemory_1_p1_9, inputmemory_1_p2_9);
  or or_3 (or_3_out, inputmemory_1_p1_8, inputmemory_1_p2_8);
  or or_4 (or_4_out, inputmemory_1_p1_7, inputmemory_1_p2_7);
  or or_5 (or_5_out, inputmemory_1_p1_6, inputmemory_1_p2_6);
  and and_1 (and_1_out, or_2_out, or_3_out, or_4_out, or_5_out, or_6_out, or_7_out, or_8_out, or_9_out, or_10_out);
  or or_6 (or_6_out, inputmemory_1_p1_5, inputmemory_1_p2_5);
  or or_7 (or_7_out, inputmemory_1_p1_4, inputmemory_1_p2_4);
  or or_8 (or_8_out, inputmemory_1_p1_3, inputmemory_1_p2_3);
  or or_9 (or_9_out, inputmemory_1_p1_2, inputmemory_1_p2_2);
  or or_10 (or_10_out, inputmemory_1_p1_1, inputmemory_1_p2_1);
  win_calc win_calc_1 (
    .key1(inputmemory_1_p1_1), .key2(inputmemory_1_p1_2), .key3(inputmemory_1_p1_3),
    .key4(inputmemory_1_p1_4), .key5(inputmemory_1_p1_5), .key6(inputmemory_1_p1_6),
    .key7(inputmemory_1_p1_7), .key8(inputmemory_1_p1_8), .key9(inputmemory_1_p1_9), .Win(win_calc_1_win));
  win_calc win_calc_2 (
    .key1(inputmemory_1_p2_1), .key2(inputmemory_1_p2_2), .key3(inputmemory_1_p2_3),
    .key4(inputmemory_1_p2_4), .key5(inputmemory_1_p2_5), .key6(inputmemory_1_p2_6),
    .key7(inputmemory_1_p2_7), .key8(inputmemory_1_p2_8), .key9(inputmemory_1_p2_9), .Win(win_calc_2_win));
  and and_2 (and_2_out, and_1_out, ~win_calc_2_win, ~win_calc_1_win);  // AND_Gate
  not not_1 (not_1_out, inputmemory_1_astate);
  or or_11 (or_11_out, win_calc_2_win, win_calc_1_win);
  LED led_1 (.in(or_11_out));
  LED led_2 (.in(or_11_out));
  LED led_3 (.in(or_11_out));
  LED led_4 (.in(or_11_out));
  LED led_5 (.in(or_11_out));
  LED led_6 (.in(or_11_out));
  LED led_7 (.in(or_11_out));
  LED led_8 (.in(or_11_out));
  LED led_9 (.in(or_11_out));
  LED led_10 (.in(and_2_out));
  LED led_11 (.in(and_2_out));
  LED led_12 (.in(and_2_out));
  LED led_13 (.in(and_2_out));
  LED led_14 (.in(and_2_out));
  LED led_15 (.in(and_2_out));
  LED led_16 (.in(and_2_out));
  LED led_17 (.in(and_2_out));
  LED led_18 (.in(and_2_out));
  LED led_19 (.in(and_2_out));
  LED led_20 (.in(and_2_out));
  LED led_21 (.in(and_2_out));
  LED led_22 (.in(or_11_out));
  LED led_23 (.in(or_11_out));
  LED led_24 (.in(or_11_out));
  LED led_25 (.in(or_11_out));
  LED led_26 (.in(or_11_out));
  LED led_27 (.in(or_11_out));
  LED led_28 (.in(inputmemory_1_p1_7));
  LED led_29 (.in(inputmemory_1_p1_7));
  LED led_30 (.in(inputmemory_1_p1_7));
  LED led_31 (.in(inputmemory_1_p2_7));
  LED led_32 (.in(inputmemory_1_p2_7));
  LED led_33 ();  // open: in
  LED led_34 (.in(inputmemory_1_p1_7));
  LED led_35 (.in(inputmemory_1_p2_7));
  LED led_36 (.in(inputmemory_1_p1_7));
  LED led_37 ();  // open: in
  LED led_38 (.in(inputmemory_1_p2_7));
  LED led_39 (.in(inputmemory_1_p2_7));
  LED led_40 (.in(inputmemory_1_p1_7));
  LED led_41 (.in(inputmemory_1_p2_7));
  LED led_42 ();  // open: in
  LED led_43 (.in(inputmemory_1_p2_7));
  LED led_44 (.in(inputmemory_1_p1_7));
  LED led_45 (.in(inputmemory_1_p1_7));
  LED led_46 (.in(inputmemory_1_p1_7));
  LED led_47 (.in(inputmemory_1_p1_4));
  LED led_48 (.in(inputmemory_1_p1_4));
  LED led_49 (.in(inputmemory_1_p1_4));
  LED led_50 (.in(inputmemory_1_p2_4));
  LED led_51 (.in(inputmemory_1_p2_4));
  LED led_52 ();  // open: in
  LED led_53 (.in(inputmemory_1_p1_4));
  LED led_54 (.in(inputmemory_1_p2_4));
  LED led_55 (.in(inputmemory_1_p1_4));
  LED led_56 ();  // open: in
  LED led_57 (.in(inputmemory_1_p2_4));
  LED led_58 (.in(inputmemory_1_p2_4));
  LED led_59 (.in(inputmemory_1_p1_4));
  LED led_60 (.in(inputmemory_1_p2_4));
  LED led_61 ();  // open: in
  LED led_62 (.in(inputmemory_1_p2_4));
  LED led_63 (.in(inputmemory_1_p1_4));
  LED led_64 (.in(inputmemory_1_p1_4));
  LED led_65 (.in(inputmemory_1_p1_4));
  LED led_66 (.in(inputmemory_1_p1_1));
  LED led_67 (.in(inputmemory_1_p1_1));
  LED led_68 (.in(inputmemory_1_p1_1));
  LED led_69 (.in(inputmemory_1_p2_1));
  LED led_70 (.in(inputmemory_1_p2_1));
  LED led_71 ();  // open: in
  LED led_72 (.in(inputmemory_1_p1_1));
  LED led_73 (.in(inputmemory_1_p2_1));
  LED led_74 (.in(inputmemory_1_p1_1));
  LED led_75 ();  // open: in
  LED led_76 (.in(inputmemory_1_p2_1));
  LED led_77 (.in(inputmemory_1_p2_1));
  LED led_78 (.in(inputmemory_1_p1_1));
  LED led_79 (.in(inputmemory_1_p2_1));
  LED led_80 ();  // open: in
  LED led_81 (.in(inputmemory_1_p2_1));
  LED led_82 (.in(inputmemory_1_p1_1));
  LED led_83 (.in(inputmemory_1_p1_1));
  LED led_84 (.in(inputmemory_1_p1_1));
  LED led_85 (.in(and_2_out));
  LED led_86 (.in(and_2_out));
  LED led_87 (.in(and_2_out));
  LED led_88 (.in(and_2_out));
  LED led_89 (.in(win_calc_1_win));
  LED led_90 (.in(inputmemory_1_p2_7));
  LED led_91 (.in(inputmemory_1_p2_8));
  LED led_92 (.in(inputmemory_1_p1_7));
  LED led_93 (.in(inputmemory_1_p1_8));
  LED led_94 ();  // open: in
  LED led_95 (.in(inputmemory_1_p1_7));
  LED led_96 (.in(inputmemory_1_p1_8));
  LED led_97 (.in(inputmemory_1_p1_7));
  LED led_98 (.in(inputmemory_1_p1_8));
  LED led_99 (.in(inputmemory_1_p2_7));
  LED led_100 (.in(inputmemory_1_p2_4));
  LED led_101 (.in(inputmemory_1_p2_5));
  LED led_102 (.in(inputmemory_1_p1_4));
  LED led_103 (.in(inputmemory_1_p1_5));
  LED led_104 ();  // open: in
  LED led_105 (.in(inputmemory_1_p1_4));
  LED led_106 (.in(inputmemory_1_p1_5));
  LED led_107 (.in(inputmemory_1_p1_4));
  LED led_108 (.in(inputmemory_1_p1_5));
  LED led_109 (.in(inputmemory_1_p2_4));
  LED led_110 (.in(inputmemory_1_p2_1));
  LED led_111 (.in(inputmemory_1_p2_2));
  LED led_112 (.in(inputmemory_1_p1_1));
  LED led_113 (.in(inputmemory_1_p1_2));
  LED led_114 ();  // open: in
  LED led_115 (.in(inputmemory_1_p1_1));
  LED led_116 (.in(inputmemory_1_p1_2));
  LED led_117 (.in(inputmemory_1_p1_1));
  LED led_118 (.in(inputmemory_1_p1_2));
  LED led_119 (.in(inputmemory_1_p2_1));
  Button n7 (.out(n7_out));
  Button n4 (.out(n4_out));
  Button n1 (.out(n1_out));
  Button RESET (.out(RESET_out));
  LED led_120 (.in(and_2_out));
  LED led_121 (.in(and_2_out));
  LED led_122 (.in(and_2_out));
  LED led_123 (.in(and_2_out));
  LED led_124 (.in(and_2_out));
  LED led_125 (.in(and_2_out));
  LED led_126 (.in(and_2_out));
  LED led_127 (.in(and_2_out));
  LED led_128 (.in(and_2_out));
  LED led_129 (.in(win_calc_1_win));
  LED led_130 (.in(win_calc_1_win));
  LED led_131 (.in(win_calc_1_win));
  LED led_132 (.in(win_calc_1_win));
  LED led_133 (.in(win_calc_1_win));
  LED led_134 (.in(win_calc_1_win));
  LED led_135 (.in(win_calc_1_win));
  LED led_136 (.in(win_calc_1_win));
  LED led_137 (.in(win_calc_1_win));
  LED led_138 (.in(win_calc_1_win));
  LED led_139 (.in(win_calc_1_win));
  LED led_140 (.in(win_calc_1_win));
  LED led_141 (.in(win_calc_1_win));
  LED led_142 (.in(inputmemory_1_p1_8));
  LED led_143 (.in(inputmemory_1_p1_8));
  LED led_144 (.in(inputmemory_1_p1_8));
  LED led_145 (.in(inputmemory_1_p2_8));
  LED led_146 (.in(inputmemory_1_p2_8));
  LED led_147 ();  // open: in
  LED led_148 (.in(inputmemory_1_p2_8));
  LED led_149 ();  // open: in
  LED led_150 (.in(inputmemory_1_p2_8));
  LED led_151 ();  // open: in
  LED led_152 (.in(inputmemory_1_p2_8));
  LED led_153 (.in(inputmemory_1_p2_8));
  LED led_154 ();  // open: in
  LED led_155 (.in(inputmemory_1_p2_8));
  LED led_156 (.in(inputmemory_1_p1_8));
  LED led_157 (.in(inputmemory_1_p1_8));
  LED led_158 (.in(inputmemory_1_p1_8));
  LED led_159 (.in(inputmemory_1_p1_5));
  LED led_160 (.in(inputmemory_1_p1_5));
  LED led_161 (.in(inputmemory_1_p1_5));
  LED led_162 (.in(inputmemory_1_p2_5));
  LED led_163 (.in(inputmemory_1_p2_5));
  LED led_164 ();  // open: in
  LED led_165 (.in(inputmemory_1_p2_5));
  LED led_166 ();  // open: in
  LED led_167 (.in(inputmemory_1_p2_5));
  LED led_168 ();  // open: in
  LED led_169 (.in(inputmemory_1_p2_5));
  LED led_170 (.in(inputmemory_1_p2_5));
  LED led_171 ();  // open: in
  LED led_172 (.in(inputmemory_1_p2_5));
  LED led_173 (.in(inputmemory_1_p1_5));
  LED led_174 (.in(inputmemory_1_p1_5));
  LED led_175 (.in(inputmemory_1_p1_5));
  LED led_176 (.in(inputmemory_1_p1_2));
  LED led_177 (.in(inputmemory_1_p1_2));
  LED led_178 (.in(inputmemory_1_p1_2));
  LED led_179 (.in(inputmemory_1_p2_2));
  LED led_180 (.in(inputmemory_1_p2_2));
  LED led_181 ();  // open: in
  LED led_182 (.in(inputmemory_1_p2_2));
  LED led_183 ();  // open: in
  LED led_184 (.in(inputmemory_1_p2_2));
  LED led_185 ();  // open: in
  LED led_186 (.in(inputmemory_1_p2_2));
  LED led_187 (.in(inputmemory_1_p2_2));
  LED led_188 ();  // open: in
  LED led_189 (.in(inputmemory_1_p2_2));
  LED led_190 (.in(inputmemory_1_p1_2));
  LED led_191 (.in(inputmemory_1_p1_2));
  LED led_192 (.in(inputmemory_1_p1_2));
  Button n8 (.out(n8_out));
  Button n5 (.out(n5_out));
  Button n2 (.out(n2_out));
  LED led_193 (.in(win_calc_1_win));
  LED led_194 (.in(inputmemory_1_p2_9));
  LED led_195 (.in(inputmemory_1_p1_8));
  LED led_196 (.in(inputmemory_1_p1_9));
  LED led_197 (.in(inputmemory_1_p1_8));
  LED led_198 (.in(inputmemory_1_p1_9));
  LED led_199 ();  // open: in
  LED led_200 (.in(inputmemory_1_p1_8));
  LED led_201 (.in(inputmemory_1_p1_9));
  LED led_202 (.in(inputmemory_1_p2_8));
  LED led_203 (.in(inputmemory_1_p2_9));
  LED led_204 (.in(inputmemory_1_p2_6));
  LED led_205 (.in(inputmemory_1_p1_5));
  LED led_206 (.in(inputmemory_1_p1_6));
  LED led_207 (.in(inputmemory_1_p1_5));
  LED led_208 (.in(inputmemory_1_p1_6));
  LED led_209 ();  // open: in
  LED led_210 (.in(inputmemory_1_p1_5));
  LED led_211 (.in(inputmemory_1_p1_6));
  LED led_212 (.in(inputmemory_1_p2_5));
  LED led_213 (.in(inputmemory_1_p2_6));
  LED led_214 (.in(inputmemory_1_p2_3));
  LED led_215 (.in(inputmemory_1_p1_2));
  LED led_216 (.in(inputmemory_1_p1_3));
  LED led_217 (.in(inputmemory_1_p1_2));
  LED led_218 (.in(inputmemory_1_p1_3));
  LED led_219 ();  // open: in
  LED led_220 (.in(inputmemory_1_p1_2));
  LED led_221 (.in(inputmemory_1_p1_3));
  LED led_222 (.in(inputmemory_1_p2_2));
  LED led_223 (.in(inputmemory_1_p2_3));
  Button n9 (.out(n9_out));
  Button n6 (.out(n6_out));
  Button n3 (.out(n3_out));
  // Switch GAME_START: pin names not known; wires that end beside it: 1'b1, GAME_START_p2
  LED led_224 (.in(and_2_out));
  LED led_225 (.in(and_2_out));
  LED led_226 (.in(and_2_out));
  LED led_227 (.in(and_2_out));
  LED led_228 (.in(and_2_out));
  LED led_229 (.in(and_2_out));
  LED led_230 (.in(and_2_out));
  LED led_231 (.in(and_2_out));
  LED led_232 (.in(and_2_out));
  LED led_233 (.in(and_2_out));
  LED led_234 (.in(and_2_out));
  LED led_235 (.in(and_2_out));
  LED led_236 (.in(and_2_out));
  LED led_237 (.in(and_2_out));
  LED led_238 (.in(and_2_out));
  LED led_239 (.in(and_2_out));
  LED led_240 (.in(and_2_out));
  LED led_241 (.in(and_2_out));
  LED led_242 (.in(win_calc_2_win));
  LED led_243 (.in(win_calc_2_win));
  LED led_244 (.in(win_calc_2_win));
  LED led_245 (.in(win_calc_2_win));
  LED led_246 (.in(win_calc_2_win));
  LED led_247 (.in(win_calc_2_win));
  LED led_248 (.in(win_calc_2_win));
  LED led_249 (.in(win_calc_2_win));
  LED led_250 (.in(win_calc_2_win));
  LED led_251 (.in(win_calc_2_win));
  LED led_252 (.in(win_calc_2_win));
  LED led_253 (.in(inputmemory_1_p1_9));
  LED led_254 (.in(inputmemory_1_p1_9));
  LED led_255 (.in(inputmemory_1_p1_9));
  LED led_256 (.in(inputmemory_1_p2_9));
  LED led_257 (.in(inputmemory_1_p2_9));
  LED led_258 ();  // open: in
  LED led_259 (.in(inputmemory_1_p2_9));
  LED led_260 (.in(inputmemory_1_p1_9));
  LED led_261 (.in(inputmemory_1_p2_9));
  LED led_262 ();  // open: in
  LED led_263 (.in(inputmemory_1_p1_9));
  LED led_264 (.in(inputmemory_1_p2_9));
  LED led_265 (.in(inputmemory_1_p2_9));
  LED led_266 ();  // open: in
  LED led_267 (.in(inputmemory_1_p1_9));
  LED led_268 (.in(inputmemory_1_p2_9));
  LED led_269 (.in(inputmemory_1_p1_9));
  LED led_270 (.in(inputmemory_1_p1_9));
  LED led_271 (.in(inputmemory_1_p1_9));
  LED led_272 (.in(inputmemory_1_p1_6));
  LED led_273 (.in(inputmemory_1_p1_6));
  LED led_274 (.in(inputmemory_1_p1_6));
  LED led_275 (.in(inputmemory_1_p2_6));
  LED led_276 (.in(inputmemory_1_p2_6));
  LED led_277 ();  // open: in
  LED led_278 (.in(inputmemory_1_p2_6));
  LED led_279 (.in(inputmemory_1_p1_6));
  LED led_280 (.in(inputmemory_1_p2_6));
  LED led_281 ();  // open: in
  LED led_282 (.in(inputmemory_1_p1_6));
  LED led_283 (.in(inputmemory_1_p2_6));
  LED led_284 (.in(inputmemory_1_p2_6));
  LED led_285 ();  // open: in
  LED led_286 (.in(inputmemory_1_p1_6));
  LED led_287 (.in(inputmemory_1_p2_6));
  LED led_288 (.in(inputmemory_1_p1_6));
  LED led_289 (.in(inputmemory_1_p1_6));
  LED led_290 (.in(inputmemory_1_p1_6));
  LED led_291 (.in(inputmemory_1_p1_3));
  LED led_292 (.in(inputmemory_1_p1_3));
  LED led_293 (.in(inputmemory_1_p1_3));
  LED led_294 (.in(inputmemory_1_p2_3));
  LED led_295 (.in(inputmemory_1_p2_3));
  LED led_296 ();  // open: in
  LED led_297 (.in(inputmemory_1_p2_3));
  LED led_298 (.in(inputmemory_1_p1_3));
  LED led_299 (.in(inputmemory_1_p2_3));
  LED led_300 ();  // open: in
  LED led_301 (.in(inputmemory_1_p1_3));
  LED led_302 (.in(inputmemory_1_p2_3));
  LED led_303 (.in(inputmemory_1_p2_3));
  LED led_304 ();  // open: in
  LED led_305 (.in(inputmemory_1_p1_3));
  LED led_306 (.in(inputmemory_1_p2_3));
  LED led_307 (.in(inputmemory_1_p1_3));
  LED led_308 (.in(inputmemory_1_p1_3));
  LED led_309 (.in(inputmemory_1_p1_3));
  LED led_310 (.in(and_2_out));
  LED led_311 (.in(and_2_out));
  LED led_312 (.in(and_2_out));
  LED led_313 (.in(and_2_out));
  LED led_314 (.in(and_2_out));
  LED led_315 (.in(and_2_out));
  LED led_316 (.in(and_2_out));
  LED led_317 (.in(and_2_out));
  LED led_318 (.in(and_2_out));
  LED led_319 (.in(win_calc_2_win));
  LED led_320 (.in(win_calc_2_win));
  LED led_321 (.in(win_calc_2_win));
  LED led_322 (.in(win_calc_2_win));
  LED led_323 (.in(win_calc_2_win));
  LED led_324 (.in(win_calc_2_win));
  LED led_325 (.in(win_calc_2_win));
  or or_12 (or_12_out, n9_out, n8_out, n7_out, n6_out, n5_out, n4_out, n3_out, n2_out, n1_out);
  or or_13 (or_13_out, or_12_out, GAME_START_p2);
  LED led_326 (.in(or_11_out));
  LED led_327 (.in(or_11_out));
  LED led_328 (.in(or_11_out));
  LED led_329 (.in(or_11_out));
  LED led_330 (.in(or_11_out));
  LED led_331 (.in(or_11_out));
  _7_Segment_Display u_7_segment_display_1 (
    .g(timer_1_t0), .f(timer_1_t1), .a(timer_1_t2), .b(timer_1_t3), .e(timer_1_b0), .d(timer_1_b1),
    .c(timer_1_b2));  // open: dp
  LED led_332 (.in(or_11_out));
  LED led_333 (.in(or_11_out));
  LED led_334 (.in(or_11_out));
  LED led_335 (.in(or_11_out));
  LED led_336 (.in(or_11_out));
  LED led_337 (.in(or_11_out));
  LED led_338 (.in(or_11_out));
  LED led_339 (.in(or_11_out));
  LED led_340 (.in(or_11_out));
  LED led_341 (.in(or_11_out));
  LED led_342 (.in(or_11_out));
  LED led_343 (.in(or_11_out));
  LED led_344 (.in(or_11_out));
  Timer timer_1 (
    .Game_Start(or_13_out), .T2(timer_1_t2), .T3(timer_1_t3), .B2(timer_1_b2), .B1(timer_1_b1),
    .B0(timer_1_b0), .T1(timer_1_t1), .T0(timer_1_t0), .TIMELIMIT(timer_1_timelimit));
  LED led_345 (.in(or_11_out));
  LED led_346 (.in(or_11_out));
  LED led_347 (.in(or_11_out));
  LED led_348 (.in(or_11_out));
  LED led_349 (.in(or_11_out));
  LED led_350 (.in(or_11_out));
  LED led_351 (.in(or_11_out));
  LED led_352 (.in(not_1_out));
  LED led_353 (.in(not_1_out));
  LED led_354 (.in(not_1_out));
  LED led_355 (.in(not_1_out));
  LED led_356 (.in(not_1_out));
  LED led_357 (.in(not_1_out));
  LED led_358 (.in(not_1_out));
  LED led_359 (.in(not_1_out));
  LED led_360 (.in(not_1_out));
  LED led_361 (.in(not_1_out));
  LED led_362 (.in(not_1_out));
  LED led_363 (.in(not_1_out));
  LED led_364 (.in(inputmemory_1_astate));
  LED led_365 (.in(inputmemory_1_astate));
  LED led_366 (.in(inputmemory_1_astate));
  LED led_367 (.in(inputmemory_1_astate));
  LED led_368 (.in(inputmemory_1_astate));
  LED led_369 (.in(inputmemory_1_astate));
  LED led_370 (.in(inputmemory_1_astate));
  LED led_371 (.in(inputmemory_1_astate));
  LED led_372 (.in(inputmemory_1_astate));
  LED led_373 (.in(inputmemory_1_astate));
  LED led_374 (.in(inputmemory_1_astate));
  LED led_375 (.in(inputmemory_1_astate));
  LED led_376 (.in(or_11_out));
  LED led_377 (.in(or_11_out));
  LED led_378 (.in(or_11_out));
  LED led_379 (.in(or_11_out));
  LED led_380 (.in(or_11_out));
  LED led_381 (.in(or_11_out));
  LED led_382 (.in(or_11_out));
  LED led_383 (.in(or_11_out));
  LED led_384 (.in(or_11_out));
  LED led_385 (.in(or_11_out));
  LED led_386 (.in(not_1_out));
  LED led_387 (.in(not_1_out));
  LED led_388 (.in(not_1_out));
  LED led_389 (.in(not_1_out));
  LED led_390 (.in(not_1_out));
  LED led_391 (.in(not_1_out));
  LED led_392 (.in(not_1_out));
  LED led_393 (.in(not_1_out));
  LED led_394 (.in(not_1_out));
  LED led_395 (.in(not_1_out));
  LED led_396 (.in(inputmemory_1_astate));
  LED led_397 (.in(inputmemory_1_astate));
  LED led_398 (.in(inputmemory_1_astate));
  LED led_399 (.in(inputmemory_1_astate));
  LED led_400 (.in(inputmemory_1_astate));
  LED led_401 (.in(inputmemory_1_astate));
  LED led_402 (.in(inputmemory_1_astate));
  LED led_403 (.in(inputmemory_1_astate));
  LED led_404 (.in(inputmemory_1_astate));
  LED led_405 (.in(inputmemory_1_astate));
  LED led_406 (.in(inputmemory_1_astate));
  LED led_407 (.in(inputmemory_1_astate));
  LED led_408 (.in(inputmemory_1_astate));
  LED led_409 (.in(inputmemory_1_astate));
  LED led_410 (.in(or_11_out));
  LED led_411 (.in(or_11_out));
  LED led_412 (.in(or_11_out));
  LED led_413 (.in(or_11_out));
  LED led_414 (.in(or_11_out));
  LED led_415 (.in(or_11_out));
  LED led_416 (.in(or_11_out));
  LED led_417 (.in(or_11_out));
  LED led_418 (.in(or_11_out));
  LED led_419 (.in(or_11_out));
  LED led_420 (.in(not_1_out));
  LED led_421 (.in(not_1_out));
  LED led_422 (.in(not_1_out));
  LED led_423 (.in(not_1_out));
  LED led_424 (.in(not_1_out));
  LED led_425 (.in(not_1_out));
  LED led_426 (.in(not_1_out));
  LED led_427 (.in(not_1_out));
  LED led_428 (.in(inputmemory_1_astate));
  LED led_429 (.in(inputmemory_1_astate));
  LED led_430 (.in(inputmemory_1_astate));
  LED led_431 (.in(inputmemory_1_astate));
  LED led_432 (.in(inputmemory_1_astate));
  LED led_433 (.in(inputmemory_1_astate));
  LED led_434 (.in(inputmemory_1_astate));
  LED led_435 (.in(not_1_out));
  LED led_436 (.in(not_1_out));
  LED led_437 (.in(not_1_out));
  LED led_438 (.in(not_1_out));
  LED led_439 (.in(not_1_out));
  LED led_440 (.in(inputmemory_1_astate));
  LED led_441 (.in(inputmemory_1_astate));
  LED led_442 (.in(inputmemory_1_astate));
  LED led_443 (.in(inputmemory_1_astate));
  LED led_444 (.in(inputmemory_1_astate));
  LED led_445 (.in(not_1_out));
  LED led_446 (.in(not_1_out));
  LED led_447 (.in(not_1_out));
  LED led_448 (.in(not_1_out));
  LED led_449 (.in(not_1_out));
  LED led_450 (.in(not_1_out));
  LED led_451 (.in(not_1_out));
  LED led_452 (.in(inputmemory_1_astate));
  LED led_453 (.in(inputmemory_1_astate));
  LED led_454 (.in(inputmemory_1_astate));
  LED led_455 (.in(inputmemory_1_astate));

  // Notes on the sheet:
  //   Time_out!!
endmodule

module downcounter (
  input  Game_Start,
  output [1:0] down_out
);

  wire clock_1_out, not_1_out, not_2_out;

  Clock clock_1 (.out(clock_1_out));
  J_K_Flip_Flop j_k_ff_1 (
    .J(1'b1), .K(1'b1), .clk(clock_1_out), .Q(down_out[0]), .preset(Game_Start));  // open: Qn, reset
  J_K_Flip_Flop j_k_ff_2 (
    .J(not_1_out), .K(not_2_out), .clk(clock_1_out), .Q(down_out[1]), .preset(Game_Start));  // open: Qn, reset
  not not_1 (not_1_out, down_out[0]);
  not not_2 (not_2_out, down_out[0]);
endmodule

module Inputmemory (
  input  d_able,
  input  k_9,
  input  k_8,
  input  k_7,
  input  k_6,
  input  k_5,
  input  k_4,
  input  k_3,
  input  k_2,
  input  k_1,
  input  reset,
  input  TimeLimit,
  output p1_9,
  output p1_8,
  output p1_7,
  output p1_6,
  output p1_5,
  output p1_4,
  output p1_3,
  output p1_2,
  output p1_1,
  output p2_9,
  output p2_8,
  output p2_7,
  output p2_6,
  output p2_5,
  output p2_4,
  output p2_3,
  output p2_2,
  output p2_1,
  output Astate
);

  wire and_1_out, and_2_out, and_3_out, and_4_out, and_5_out, and_6_out, and_7_out, and_8_out, and_9_out,
       and_10_out, and_11_out, bitcounter_1_1_value, bitcounter_1_2_value, d_latch_lock_2_1_q,
       d_latch_lock_2_2_q, d_latch_lock_2_3_q, d_latch_lock_2_4_q, d_latch_lock_2_5_q, d_latch_lock_2_6_q,
       d_latch_lock_2_7_q, d_latch_lock_2_8_q, d_latch_lock_2_9_q, or_1_out, or_2_out,
       playerswitch_1_player1, playerswitch_1_player2, playerswitch_2_player1, playerswitch_2_player2,
       playerswitch_3_player1, playerswitch_3_player2, playerswitch_4_player1, playerswitch_4_player2,
       playerswitch_5_player1, playerswitch_5_player2, playerswitch_6_player1, playerswitch_6_player2,
       playerswitch_7_player1, playerswitch_7_player2, playerswitch_8_player1, playerswitch_8_player2,
       playerswitch_9_player1, playerswitch_9_player2, xnor_1_out, xor_1_out, xor_2_out;

  D_latch_lock_2 d_latch_lock_2_1 (.D(k_9), .WE(reset), .Q(d_latch_lock_2_1_q));
  D_latch_lock_2 d_latch_lock_2_2 (.D(k_8), .WE(reset), .Q(d_latch_lock_2_2_q));
  D_latch_lock_2 d_latch_lock_2_3 (.D(k_7), .WE(reset), .Q(d_latch_lock_2_3_q));
  D_latch_lock_2 d_latch_lock_2_4 (.D(k_6), .WE(reset), .Q(d_latch_lock_2_4_q));
  D_latch_lock_2 d_latch_lock_2_5 (.D(k_5), .WE(reset), .Q(d_latch_lock_2_5_q));
  D_latch_lock_2 d_latch_lock_2_6 (.D(k_4), .WE(reset), .Q(d_latch_lock_2_6_q));
  D_latch_lock_2 d_latch_lock_2_7 (.D(k_3), .WE(reset), .Q(d_latch_lock_2_7_q));
  D_latch_lock_2 d_latch_lock_2_8 (.D(k_2), .WE(reset), .Q(d_latch_lock_2_8_q));
  D_latch_lock_2 d_latch_lock_2_9 (.D(k_1), .WE(reset), .Q(d_latch_lock_2_9_q));
  xnor xnor_1 (xnor_1_out, d_able, reset);
  and and_1 (and_1_out, ~d_latch_lock_2_1_q, k_9);  // AND_Gate
  and and_2 (and_2_out, ~d_latch_lock_2_2_q, k_8);  // AND_Gate
  and and_3 (and_3_out, ~d_latch_lock_2_3_q, k_7);  // AND_Gate
  and and_4 (and_4_out, ~d_latch_lock_2_4_q, k_6);  // AND_Gate
  and and_5 (and_5_out, ~d_latch_lock_2_5_q, k_5);  // AND_Gate
  and and_6 (and_6_out, ~d_latch_lock_2_6_q, k_4);  // AND_Gate
  and and_7 (and_7_out, ~d_latch_lock_2_7_q, k_3);  // AND_Gate
  and and_8 (and_8_out, ~d_latch_lock_2_8_q, k_2);  // AND_Gate
  and and_9 (and_9_out, ~d_latch_lock_2_9_q, k_1);  // AND_Gate
  playerswitch playerswitch_1 (
    .key(d_latch_lock_2_1_q), .switch(Astate), .player1(playerswitch_1_player1),
    .player2(playerswitch_1_player2));
  playerswitch playerswitch_2 (
    .key(d_latch_lock_2_2_q), .switch(Astate), .player1(playerswitch_2_player1),
    .player2(playerswitch_2_player2));
  playerswitch playerswitch_3 (
    .key(d_latch_lock_2_3_q), .switch(Astate), .player1(playerswitch_3_player1),
    .player2(playerswitch_3_player2));
  playerswitch playerswitch_4 (
    .key(d_latch_lock_2_4_q), .switch(Astate), .player1(playerswitch_4_player1),
    .player2(playerswitch_4_player2));
  playerswitch playerswitch_5 (
    .key(d_latch_lock_2_5_q), .switch(Astate), .player1(playerswitch_5_player1),
    .player2(playerswitch_5_player2));
  playerswitch playerswitch_6 (
    .key(d_latch_lock_2_6_q), .switch(Astate), .player1(playerswitch_6_player1),
    .player2(playerswitch_6_player2));
  playerswitch playerswitch_7 (
    .key(d_latch_lock_2_7_q), .switch(Astate), .player1(playerswitch_7_player1),
    .player2(playerswitch_7_player2));
  playerswitch playerswitch_8 (
    .key(d_latch_lock_2_8_q), .switch(Astate), .player1(playerswitch_8_player1),
    .player2(playerswitch_8_player2));
  playerswitch playerswitch_9 (
    .key(d_latch_lock_2_9_q), .switch(Astate), .player1(playerswitch_9_player1),
    .player2(playerswitch_9_player2));
  or or_1 (or_1_out, and_1_out, and_2_out, and_3_out, and_4_out, and_5_out, and_6_out, and_7_out, and_8_out, and_9_out);
  D_Flip_Flop #(.trigger("high")) d_ff_1 (
    .D(playerswitch_1_player1), .clk(xnor_1_out), .Q(p1_9));  // open: Qn, preset, reset
  D_Flip_Flop #(.trigger("high")) d_ff_2 (
    .D(playerswitch_2_player2), .clk(xnor_1_out), .Q(p2_8));  // open: Qn, preset, reset
  D_Flip_Flop #(.trigger("high")) d_ff_3 (
    .D(playerswitch_3_player2), .clk(xnor_1_out), .Q(p2_7));  // open: Qn, preset, reset
  D_Flip_Flop #(.trigger("high")) d_ff_4 (
    .D(playerswitch_1_player2), .clk(xnor_1_out), .Q(p2_9));  // open: Qn, preset, reset
  D_Flip_Flop #(.trigger("high")) d_ff_5 (
    .D(playerswitch_4_player2), .clk(xnor_1_out), .Q(p2_6));  // open: Qn, preset, reset
  D_Flip_Flop #(.trigger("high")) d_ff_6 (
    .D(playerswitch_5_player2), .clk(xnor_1_out), .Q(p2_5));  // open: Qn, preset, reset
  D_Flip_Flop #(.trigger("high")) d_ff_7 (
    .D(playerswitch_6_player2), .clk(xnor_1_out), .Q(p2_4));  // open: Qn, preset, reset
  D_Flip_Flop #(.trigger("high")) d_ff_8 (
    .D(playerswitch_7_player2), .clk(xnor_1_out), .Q(p2_3));  // open: Qn, preset, reset
  D_Flip_Flop #(.trigger("high")) d_ff_9 (
    .D(playerswitch_8_player2), .clk(xnor_1_out), .Q(p2_2));  // open: Qn, preset, reset
  D_Flip_Flop #(.trigger("high")) d_ff_10 (
    .D(playerswitch_9_player2), .clk(xnor_1_out), .Q(p2_1));  // open: Qn, preset, reset
  D_Flip_Flop #(.trigger("high")) d_ff_11 (
    .D(playerswitch_2_player1), .clk(xnor_1_out), .Q(p1_8));  // open: Qn, preset, reset
  D_Flip_Flop #(.trigger("high")) d_ff_12 (
    .D(playerswitch_4_player1), .clk(xnor_1_out), .Q(p1_6));  // open: Qn, preset, reset
  bitcounter_1 bitcounter_1_1 (
    .maxvalue(1'b1), .clock(or_1_out), .reset(reset), .value(bitcounter_1_1_value));  // open: zero
  D_Flip_Flop #(.trigger("high")) d_ff_13 (
    .D(playerswitch_3_player1), .clk(xnor_1_out), .Q(p1_7));  // open: Qn, preset, reset
  D_Flip_Flop #(.trigger("high")) d_ff_14 (
    .D(playerswitch_5_player1), .clk(xnor_1_out), .Q(p1_5));  // open: Qn, preset, reset
  D_Flip_Flop #(.trigger("high")) d_ff_15 (
    .D(playerswitch_6_player1), .clk(xnor_1_out), .Q(p1_4));  // open: Qn, preset, reset
  D_Flip_Flop #(.trigger("high")) d_ff_16 (
    .D(playerswitch_7_player1), .clk(xnor_1_out), .Q(p1_3));  // open: Qn, preset, reset
  D_Flip_Flop #(.trigger("high")) d_ff_17 (
    .D(playerswitch_8_player1), .clk(xnor_1_out), .Q(p1_2));  // open: Qn, preset, reset
  D_Flip_Flop #(.trigger("high")) d_ff_18 (
    .D(playerswitch_9_player1), .clk(xnor_1_out), .Q(p1_1));  // open: Qn, preset, reset
  bitcounter_1 bitcounter_1_2 (
    .maxvalue(1'b1), .clock(TimeLimit), .reset(reset), .value(bitcounter_1_2_value));  // open: zero
  or or_2 (or_2_out, xor_1_out, and_10_out);
  xor xor_1 (xor_1_out, bitcounter_1_1_value, bitcounter_1_2_value);
  and and_10 (and_10_out, bitcounter_1_1_value, bitcounter_1_2_value);
  and and_11 (and_11_out, bitcounter_1_2_value, bitcounter_1_1_value);
  xor xor_2 (xor_2_out, or_2_out, and_11_out);
  D_Flip_Flop #(.trigger("high")) d_ff_19 (.D(xor_2_out), .clk(xnor_1_out), .Q(Astate));  // open: Qn, preset, reset
endmodule

module playerswitch (
  input  key,
  input  switch,
  output player1,
  output player2
);

  wire and_1_out, d_ff_1_q, xnor_1_out;

  and and_1 (and_1_out, key, xnor_1_out);
  D_Flip_Flop d_ff_1 (.D(switch), .clk(and_1_out), .Q(d_ff_1_q));  // open: Qn, preset, reset
  Demultiplexer demultiplexer_1 (.out0(player1), .out1(player2), .in(key), .sel(d_ff_1_q));
  xnor xnor_1 (xnor_1_out, player1, player2);
endmodule

module D_latch_lock_2 (
  input  D,
  input  WE,
  output Q
);

  wire or_1_out;

  or or_1 (or_1_out, D, WE);
  D_Flip_Flop d_ff_1 (.D(D), .clk(or_1_out), .Q(Q));  // open: Qn, preset, reset
endmodule

module win_calc (
  input  key1,
  input  key2,
  input  key3,
  input  key4,
  input  key5,
  input  key6,
  input  key7,
  input  key8,
  input  key9,
  output Win
);

  wire A123_out, A147_out, A159_out, A258_out, A357_out, A369_out, A456_out, A789_out;

  and A123 (A123_out, key1, key2, key3);
  and A456 (A456_out, key4, key5, key6);
  and A789 (A789_out, key7, key8, key9);
  and A147 (A147_out, key1, key4, key7);
  and A258 (A258_out, key2, key5, key8);
  and A369 (A369_out, key3, key6, key9);
  and A159 (A159_out, key1, key5, key9);
  and A357 (A357_out, key3, key5, key7);
  or or_1 (Win, A123_out, A456_out, A789_out, A147_out, A258_out, A369_out, A159_out, A357_out);
endmodule

module bitcounter_1 (
  input  maxvalue,
  input  clock,
  input  reset,
  output value,
  output zero
);

  Counter #(.max('h1), .width(1)) counter_1 (
    .D(maxvalue), .count(1'b1), .Q(value), .carry(zero), .up(1'b1), .clk(clock), .clr(reset));  // open: load
endmodule

module Timer (
  input  Game_Start,
  output T2,
  output T3,
  output B2,
  output B1,
  output B0,
  output T1,
  output T0,
  output TIMELIMIT
);

  wire [1:0] downcounter_1_down_out;

  downcounter downcounter_1 (.Game_Start(Game_Start), .down_out(downcounter_1_down_out));
  // PlaRom #(.Contents("2 2 1 2 2 1*3 1*4 0 0 1 0 1 1 0*4 1 1 0 1 1 0 1*7 0"), .outputs(7)) plarom_1: pin names not known; wires that end beside it: downcounter_1_down_out, {T2, T3, B2, B1, B0, T1, T0}
  and TIME_OUT (TIMELIMIT, T2, T3, B2, B1, B0, T1);
endmodule
