// Logisim project dlatch_tictactoc.circ as structural Verilog: 9 circuits, main circuit main
module main (
);

  wire inputmemory_1_astate, n1_out, n2_out, n3_out, n4_out, n5_out, n6_out, n7_out, n8_out, n9_out,
       not_1_out, restart_out;

  Inputmemory inputmemory_1 (
    .k_9(n9_out), .k_8(n8_out), .k_7(n7_out), .k_6(n6_out), .k_5(n5_out), .k_4(n4_out), .k_3(n3_out),
    .k_2(n2_out), .k_1(n1_out), .reset(restart_out), .Astate(inputmemory_1_astate));  // open: d_able, p1_9, p1_8, p1_7, p1_6, p1_5, p1_4, p1_3, p1_2, p1_1, p2_9, p2_8, p2_7, p2_6, p2_5, p2_4, p2_3, p2_2, p2_1
  win_calc win_calc_1 ();  // open: in_1, in_2, in_3, in_4, in_5, in_6, in_7, in_8, in_9, Win
  win_calc win_calc_2 ();  // open: in_1, in_2, in_3, in_4, in_5, in_6, in_7, in_8, in_9, Win
  not not_1 (not_1_out, inputmemory_1_astate);
  DotMatrix #(.inputtype("row"), .matrixcols(3), .matrixrows(3)) dotmatrix_1 ();  // open: row0, row1, row2
  DotMatrix #(.inputtype("row"), .matrixcols(3), .matrixrows(3)) dotmatrix_2 ();  // open: row0, row1, row2
  DotMatrix #(.inputtype("row"), .matrixcols(3), .matrixrows(3)) dotmatrix_3 ();  // open: row0, row1, row2
  DotMatrix #(.inputtype("row"), .matrixcols(3), .matrixrows(3)) dotmatrix_4 ();  // open: row0, row1, row2
  DotMatrix #(.inputtype("row"), .matrixcols(3), .matrixrows(3)) dotmatrix_5 ();  // open: row0, row1, row2
  DotMatrix #(.inputtype("row"), .matrixcols(3), .matrixrows(3)) dotmatrix_6 ();  // open: row0, row1, row2
  DotMatrix #(.inputtype("row"), .matrixcols(3), .matrixrows(3)) dotmatrix_7 ();  // open: row0, row1, row2
  DotMatrix #(.inputtype("row"), .matrixcols(3), .matrixrows(3)) dotmatrix_8 ();  // open: row0, row1, row2
  DotMatrix #(.inputtype("row"), .matrixcols(3), .matrixrows(3)) dotmatrix_9 ();  // open: row0, row1, row2
  DotMatrix #(.inputtype("row"), .matrixcols(3), .matrixrows(3)) dotmatrix_10 ();  // open: row0, row1, row2
  DotMatrix #(.inputtype("row"), .matrixcols(3), .matrixrows(3)) dotmatrix_11 ();  // open: row0, row1, row2
  DotMatrix #(.inputtype("row"), .matrixcols(3), .matrixrows(3)) dotmatrix_12 ();  // open: row0, row1, row2
  DotMatrix #(.inputtype("row"), .matrixcols(3), .matrixrows(3)) dotmatrix_13 ();  // open: row0, row1, row2
  DotMatrix #(.inputtype("row"), .matrixcols(3), .matrixrows(3)) dotmatrix_14 ();  // open: row0, row1, row2
  DotMatrix #(.inputtype("row"), .matrixcols(3), .matrixrows(3)) dotmatrix_15 ();  // open: row0, row1, row2
  DotMatrix #(.inputtype("row"), .matrixcols(3), .matrixrows(3)) dotmatrix_16 ();  // open: row0, row1, row2
  DotMatrix #(.inputtype("row"), .matrixcols(3), .matrixrows(3)) dotmatrix_17 ();  // open: row0, row1, row2
  DotMatrix #(.inputtype("row"), .matrixcols(3), .matrixrows(3)) dotmatrix_18 ();  // open: row0, row1, row2
  DotMatrix #(.inputtype("row"), .matrixcols(3), .matrixrows(3)) dotmatrix_19 ();  // open: row0, row1, row2
  DotMatrix #(.inputtype("row"), .matrixcols(3), .matrixrows(3)) dotmatrix_20 ();  // open: row0, row1, row2
  DotMatrix #(.inputtype("row"), .matrixcols(3), .matrixrows(3)) dotmatrix_21 ();  // open: row0, row1, row2
  DotMatrix #(.inputtype("row"), .matrixcols(3), .matrixrows(3)) dotmatrix_22 ();  // open: row0, row1, row2
  DotMatrix #(.inputtype("row"), .matrixcols(3), .matrixrows(3)) dotmatrix_23 ();  // open: row0, row1, row2
  DotMatrix #(.inputtype("row"), .matrixcols(3), .matrixrows(3)) dotmatrix_24 ();  // open: row0, row1, row2
  DotMatrix #(.inputtype("row"), .matrixcols(3), .matrixrows(3)) dotmatrix_25 ();  // open: row0, row1, row2
  DotMatrix #(.inputtype("row"), .matrixcols(3), .matrixrows(3)) dotmatrix_26 ();  // open: row0, row1, row2
  DotMatrix #(.inputtype("row"), .matrixcols(3), .matrixrows(3)) dotmatrix_27 ();  // open: row0, row1, row2
  Button n7 (.out(n7_out));
  Button n4 (.out(n4_out));
  Button n1 (.out(n1_out));
  Button restart (.out(restart_out));
  DotMatrix #(.inputtype("row"), .matrixcols(3), .matrixrows(3)) dotmatrix_28 ();  // open: row0, row1, row2
  DotMatrix #(.inputtype("row"), .matrixcols(3), .matrixrows(3)) dotmatrix_29 ();  // open: row0, row1, row2
  DotMatrix #(.inputtype("row"), .matrixcols(3), .matrixrows(3)) dotmatrix_30 ();  // open: row0, row1, row2
  DotMatrix #(.inputtype("row"), .matrixcols(3), .matrixrows(3)) dotmatrix_31 ();  // open: row0, row1, row2
  DotMatrix #(.inputtype("row"), .matrixcols(3), .matrixrows(3)) dotmatrix_32 ();  // open: row0, row1, row2
  DotMatrix #(.inputtype("row"), .matrixcols(3), .matrixrows(3)) dotmatrix_33 ();  // open: row0, row1, row2
  DotMatrix #(.inputtype("row"), .matrixcols(3), .matrixrows(3)) dotmatrix_34 ();  // open: row0, row1, row2
  DotMatrix #(.inputtype("row"), .matrixcols(3), .matrixrows(3)) dotmatrix_35 ();  // open: row0, row1, row2
  DotMatrix #(.inputtype("row"), .matrixcols(3), .matrixrows(3)) dotmatrix_36 ();  // open: row0, row1, row2
  DotMatrix #(.inputtype("row"), .matrixcols(3), .matrixrows(3)) dotmatrix_37 ();  // open: row0, row1, row2
  DotMatrix #(.inputtype("row"), .matrixcols(3), .matrixrows(3)) dotmatrix_38 ();  // open: row0, row1, row2
  DotMatrix #(.inputtype("row"), .matrixcols(3), .matrixrows(3)) dotmatrix_39 ();  // open: row0, row1, row2
  DotMatrix #(.inputtype("row"), .matrixcols(3), .matrixrows(3)) dotmatrix_40 ();  // open: row0, row1, row2
  DotMatrix #(.inputtype("row"), .matrixcols(3), .matrixrows(3)) dotmatrix_41 ();  // open: row0, row1, row2
  DotMatrix #(.inputtype("row"), .matrixcols(3), .matrixrows(3)) dotmatrix_42 ();  // open: row0, row1, row2
  DotMatrix #(.inputtype("row"), .matrixcols(3), .matrixrows(3)) dotmatrix_43 ();  // open: row0, row1, row2
  DotMatrix #(.inputtype("row"), .matrixcols(3), .matrixrows(3)) dotmatrix_44 ();  // open: row0, row1, row2
  DotMatrix #(.inputtype("row"), .matrixcols(3), .matrixrows(3)) dotmatrix_45 ();  // open: row0, row1, row2
  Button n8 (.out(n8_out));
  Button n5 (.out(n5_out));
  Button n2 (.out(n2_out));
  DotMatrix #(.inputtype("row"), .matrixcols(3), .matrixrows(3)) dotmatrix_46 ();  // open: row0, row1, row2
  DotMatrix #(.inputtype("row"), .matrixcols(3), .matrixrows(3)) dotmatrix_47 ();  // open: row0, row1, row2
  DotMatrix #(.inputtype("row"), .matrixcols(3), .matrixrows(3)) dotmatrix_48 ();  // open: row0, row1, row2
  DotMatrix #(.inputtype("row"), .matrixcols(3), .matrixrows(3)) dotmatrix_49 ();  // open: row0, row1, row2
  DotMatrix #(.inputtype("row"), .matrixcols(3), .matrixrows(3)) dotmatrix_50 ();  // open: row0, row1, row2
  DotMatrix #(.inputtype("row"), .matrixcols(3), .matrixrows(3)) dotmatrix_51 ();  // open: row0, row1, row2
  DotMatrix #(.inputtype("row"), .matrixcols(3), .matrixrows(3)) dotmatrix_52 ();  // open: row0, row1, row2
  DotMatrix #(.inputtype("row"), .matrixcols(3), .matrixrows(3)) dotmatrix_53 ();  // open: row0, row1, row2
  DotMatrix #(.inputtype("row"), .matrixcols(3), .matrixrows(3)) dotmatrix_54 ();  // open: row0, row1, row2
  Button n9 (.out(n9_out));
  Button n6 (.out(n6_out));
  Button n3 (.out(n3_out));
  DotMatrix #(.inputtype("row"), .matrixcols(3), .matrixrows(3)) dotmatrix_55 ();  // open: row0, row1, row2
  DotMatrix #(.inputtype("row"), .matrixcols(3), .matrixrows(3)) dotmatrix_56 ();  // open: row0, row1, row2
  DotMatrix #(.inputtype("row"), .matrixcols(3), .matrixrows(3)) dotmatrix_57 ();  // open: row0, row1, row2
  DotMatrix #(.inputtype("row"), .matrixcols(3), .matrixrows(3)) dotmatrix_58 ();  // open: row0, row1, row2
  DotMatrix #(.inputtype("row"), .matrixcols(3), .matrixrows(3)) dotmatrix_59 ();  // open: row0, row1, row2
  DotMatrix #(.inputtype("row"), .matrixcols(3), .matrixrows(3)) dotmatrix_60 ();  // open: row0, row1, row2
  DotMatrix #(.inputtype("row"), .matrixcols(3), .matrixrows(3)) dotmatrix_61 ();  // open: row0, row1, row2
  DotMatrix #(.inputtype("row"), .matrixcols(3), .matrixrows(3)) dotmatrix_62 ();  // open: row0, row1, row2
  DotMatrix #(.inputtype("row"), .matrixcols(3), .matrixrows(3)) dotmatrix_63 ();  // open: row0, row1, row2
  DotMatrix #(.inputtype("row"), .matrixcols(3), .matrixrows(3)) dotmatrix_64 ();  // open: row0, row1, row2
  DotMatrix #(.inputtype("row"), .matrixcols(3), .matrixrows(3)) dotmatrix_65 ();  // open: row0, row1, row2
  DotMatrix #(.inputtype("row"), .matrixcols(3), .matrixrows(3)) dotmatrix_66 ();  // open: row0, row1, row2
  DotMatrix #(.inputtype("row"), .matrixcols(3), .matrixrows(3)) dotmatrix_67 ();  // open: row0, row1, row2
  DotMatrix #(.inputtype("row"), .matrixcols(3), .matrixrows(3)) dotmatrix_68 ();  // open: row0, row1, row2
  DotMatrix #(.inputtype("row"), .matrixcols(3), .matrixrows(3)) dotmatrix_69 ();  // open: row0, row1, row2
  DotMatrix #(.inputtype("row"), .matrixcols(3), .matrixrows(3)) dotmatrix_70 ();  // open: row0, row1, row2
  DotMatrix #(.inputtype("row"), .matrixcols(3), .matrixrows(3)) dotmatrix_71 ();  // open: row0, row1, row2
  DotMatrix #(.inputtype("row"), .matrixcols(3), .matrixrows(3)) dotmatrix_72 ();  // open: row0, row1, row2
  DotMatrix #(.inputtype("row"), .matrixcols(3), .matrixrows(3)) dotmatrix_73 ();  // open: row0, row1, row2
  DotMatrix #(.inputtype("row"), .matrixcols(3), .matrixrows(3)) dotmatrix_74 ();  // open: row0, row1, row2
  DotMatrix #(.inputtype("row"), .matrixcols(3), .matrixrows(3)) dotmatrix_75 ();  // open: row0, row1, row2
  DotMatrix #(.inputtype("row"), .matrixcols(3), .matrixrows(3)) dotmatrix_76 ();  // open: row0, row1, row2
  DotMatrix #(.inputtype("row"), .matrixcols(3), .matrixrows(3)) dotmatrix_77 ();  // open: row0, row1, row2
  DotMatrix #(.inputtype("row"), .matrixcols(3), .matrixrows(3)) dotmatrix_78 ();  // open: row0, row1, row2
  DotMatrix #(.inputtype("row"), .matrixcols(3), .matrixrows(3)) dotmatrix_79 ();  // open: row0, row1, row2
  DotMatrix #(.inputtype("row"), .matrixcols(3), .matrixrows(3)) dotmatrix_80 ();  // open: row0, row1, row2
  DotMatrix #(.inputtype("row"), .matrixcols(3), .matrixrows(3)) dotmatrix_81 ();  // open: row0, row1, row2
  LED led_1 (.in(inputmemory_1_astate));
  LED led_2 (.in(inputmemory_1_astate));
  LED led_3 (.in(inputmemory_1_astate));
  LED led_4 (.in(inputmemory_1_astate));
  LED led_5 (.in(inputmemory_1_astate));
  LED led_6 (.in(inputmemory_1_astate));
  LED led_7 (.in(inputmemory_1_astate));
  LED led_8 (.in(inputmemory_1_astate));
  LED led_9 (.in(inputmemory_1_astate));
  LED led_10 (.in(inputmemory_1_astate));
  LED led_11 (.in(inputmemory_1_astate));
  LED led_12 (.in(inputmemory_1_astate));
  LED led_13 (.in(inputmemory_1_astate));
  LED led_14 (.in(not_1_out));
  LED led_15 (.in(not_1_out));
  LED led_16 (.in(not_1_out));
  LED led_17 (.in(not_1_out));
  LED led_18 (.in(not_1_out));
  LED led_19 (.in(not_1_out));
  LED led_20 (.in(not_1_out));
  LED led_21 (.in(not_1_out));
  LED led_22 (.in(not_1_out));
  LED led_23 (.in(not_1_out));
  LED led_24 (.in(not_1_out));
  LED led_25 (.in(not_1_out));
  LED led_26 (.in(not_1_out));
  LED led_27 (.in(inputmemory_1_astate));
  LED led_28 (.in(inputmemory_1_astate));
  LED led_29 (.in(inputmemory_1_astate));
  LED led_30 (.in(inputmemory_1_astate));
  LED led_31 (.in(inputmemory_1_astate));
  LED led_32 (.in(inputmemory_1_astate));
  LED led_33 (.in(inputmemory_1_astate));
  LED led_34 (.in(inputmemory_1_astate));
  // RGBLED rgbled_1: pin names not known; wires that end beside it: inputmemory_1_astate, not_1_out, not_1_out, inputmemory_1_astate, not_1_out
  LED led_35 (.in(inputmemory_1_astate));
  LED led_36 (.in(inputmemory_1_astate));
  LED led_37 (.in(inputmemory_1_astate));
  LED led_38 (.in(inputmemory_1_astate));
  LED led_39 (.in(inputmemory_1_astate));
  LED led_40 (.in(inputmemory_1_astate));
  LED led_41 (.in(inputmemory_1_astate));
  LED led_42 (.in(not_1_out));
  LED led_43 (.in(not_1_out));
  LED led_44 (.in(not_1_out));
  LED led_45 (.in(not_1_out));
  LED led_46 (.in(not_1_out));
  LED led_47 (.in(not_1_out));
  LED led_48 (.in(not_1_out));
  LED led_49 (.in(not_1_out));
  LED led_50 (.in(not_1_out));
  LED led_51 (.in(not_1_out));
  LED led_52 (.in(not_1_out));
  LED led_53 (.in(not_1_out));
  LED led_54 (.in(not_1_out));
  LED led_55 (.in(not_1_out));
  LED led_56 (.in(inputmemory_1_astate));
  LED led_57 (.in(inputmemory_1_astate));
  LED led_58 (.in(not_1_out));
  LED led_59 (.in(not_1_out));
  LED led_60 (.in(not_1_out));
  LED led_61 (.in(not_1_out));
  LED led_62 (.in(not_1_out));
  LED led_63 (.in(not_1_out));
endmodule

module D_latch (
  input  D,
  input  Enable,
  output Q,
  output notQ
);

  wire and_1_out, and_2_out, not_1_out;

  not not_1 (not_1_out, D);
  and and_1 (and_1_out, not_1_out, Enable);
  and and_2 (and_2_out, Enable, D);
  nor nor_1 (Q, and_1_out, notQ);
  nor nor_2 (notQ, Q, and_2_out);
endmodule

module playerswitch (
  input  key,
  input  switch,
  output player1,
  output player2
);

  wire and_1_out, d_latch_1_q, xnor_1_out;

  and and_1 (and_1_out, key, xnor_1_out);
  Demultiplexer demultiplexer_1 (.out0(player1), .out1(player2), .in(key), .sel(d_latch_1_q));
  D_latch d_latch_1 (.D(switch), .Enable(and_1_out), .Q(d_latch_1_q));  // open: notQ
  xnor xnor_1 (xnor_1_out, player1, player2);
endmodule

module D_latch_lock (
  input  D,
  input  WE,
  output Q
);

  wire d_latch_1_q, or_1_out;

  or or_1 (or_1_out, D, WE);
  not not_1 (Q, d_latch_1_q);
  D_latch d_latch_1 (.D(D), .Enable(or_1_out), .Q(d_latch_1_q));  // open: notQ
endmodule

module D_latch_lock_2 (
  input  D,
  input  WE,
  output Q
);

  wire or_1_out;

  or or_1 (or_1_out, D, WE);
  D_latch d_latch_1 (.D(D), .Enable(or_1_out), .Q(Q));  // open: notQ
endmodule

module RGB_selector (
  input  p1,
  input  p2,
  output [7:0] out_3,
  output [7:0] out_4
);

  Multiplexer #(.width(8)) multiplexer_1 (.in0({8{1'b0}}), .in1({8{1'b1}}), .out(out_3), .sel(p1));
  Multiplexer #(.width(8)) multiplexer_2 (.in0({8{1'b0}}), .in1({8{1'b1}}), .out(out_4), .sel(p2));
endmodule

module Inputmemory (
  input  d_able,
  input  k_9,
  input  k_8,
  input  k_7,
  input  k_6,
  input  k_5,
  input  k_4,
  input  k_3,
  input  k_2,
  input  k_1,
  input  reset,
  output p1_9,
  output p1_8,
  output p1_7,
  output p1_6,
  output p1_5,
  output p1_4,
  output p1_3,
  output p1_2,
  output p1_1,
  output p2_9,
  output p2_8,
  output p2_7,
  output p2_6,
  output p2_5,
  output p2_4,
  output p2_3,
  output p2_2,
  output p2_1,
  output Astate
);

  wire and_1_out, and_2_out, and_3_out, and_4_out, and_5_out, and_6_out, and_7_out, and_8_out, and_9_out,
       bitcounter_1_1_value, d_latch_lock_2_1_q, d_latch_lock_2_2_q, d_latch_lock_2_3_q, d_latch_lock_2_4_q,
       d_latch_lock_2_5_q, d_latch_lock_2_6_q, d_latch_lock_2_7_q, d_latch_lock_2_8_q, d_latch_lock_2_9_q,
       or_1_out, playerswitch_1_player1, playerswitch_1_player2, playerswitch_2_player1,
       playerswitch_2_player2, playerswitch_3_player1, playerswitch_3_player2, playerswitch_4_player1,
       playerswitch_4_player2, playerswitch_5_player1, playerswitch_5_player2, playerswitch_6_player1,
       playerswitch_6_player2, playerswitch_7_player1, playerswitch_7_player2, playerswitch_8_player1,
       playerswitch_8_player2, playerswitch_9_player1, playerswitch_9_player2, xnor_1_out;

  D_latch_lock_2 d_latch_lock_2_1 (.D(k_9), .WE(reset), .Q(d_latch_lock_2_1_q));
  D_latch_lock_2 d_latch_lock_2_2 (.D(k_8), .WE(reset), .Q(d_latch_lock_2_2_q));
  D_latch_lock_2 d_latch_lock_2_3 (.D(k_7), .WE(reset), .Q(d_latch_lock_2_3_q));
  D_latch_lock_2 d_latch_lock_2_4 (.D(k_6), .WE(reset), .Q(d_latch_lock_2_4_q));
  D_latch_lock_2 d_latch_lock_2_5 (.D(k_5), .WE(reset), .Q(d_latch_lock_2_5_q));
  D_latch_lock_2 d_latch_lock_2_6 (.D(k_4), .WE(reset), .Q(d_latch_lock_2_6_q));
  D_latch_lock_2 d_latch_lock_2_7 (.D(k_3), .WE(reset), .Q(d_latch_lock_2_7_q));
  D_latch_lock_2 d_latch_lock_2_8 (.D(k_2), .WE(reset), .Q(d_latch_lock_2_8_q));
  D_latch_lock_2 d_latch_lock_2_9 (.D(k_1), .WE(reset), .Q(d_latch_lock_2_9_q));
  xnor xnor_1 (xnor_1_out, d_able, reset);
  and and_1 (and_1_out, ~d_latch_lock_2_1_q, k_9);  // AND_Gate
  and and_2 (and_2_out, ~d_latch_lock_2_2_q, k_8);  // AND_Gate
  and and_3 (and_3_out, ~d_latch_lock_2_3_q, k_7);  // AND_Gate
  and and_4 (and_4_out, ~d_latch_lock_2_4_q, k_6);  // AND_Gate
  and and_5 (and_5_out, ~d_latch_lock_2_5_q, k_5);  // AND_Gate
  and and_6 (and_6_out, ~d_latch_lock_2_6_q, k_4);  // AND_Gate
  and and_7 (and_7_out, ~d_latch_lock_2_7_q, k_3);  // AND_Gate
  and and_8 (and_8_out, ~d_latch_lock_2_8_q, k_2);  // AND_Gate
  and and_9 (and_9_out, ~d_latch_lock_2_9_q, k_1);  // AND_Gate
  playerswitch playerswitch_1 (
    .key(d_latch_lock_2_1_q), .switch(bitcounter_1_1_value), .player1(playerswitch_1_player1),
    .player2(playerswitch_1_player2));
  playerswitch playerswitch_2 (
    .key(d_latch_lock_2_2_q), .switch(bitcounter_1_1_value), .player1(playerswitch_2_player1),
    .player2(playerswitch_2_player2));
  playerswitch playerswitch_3 (
    .key(d_latch_lock_2_3_q), .switch(bitcounter_1_1_value), .player1(playerswitch_3_player1),
    .player2(playerswitch_3_player2));
  playerswitch playerswitch_4 (
    .key(d_latch_lock_2_4_q), .switch(bitcounter_1_1_value), .player1(playerswitch_4_player1),
    .player2(playerswitch_4_player2));
  playerswitch playerswitch_5 (
    .key(d_latch_lock_2_5_q), .switch(bitcounter_1_1_value), .player1(playerswitch_5_player1),
    .player2(playerswitch_5_player2));
  playerswitch playerswitch_6 (
    .key(d_latch_lock_2_6_q), .switch(bitcounter_1_1_value), .player1(playerswitch_6_player1),
    .player2(playerswitch_6_player2));
  playerswitch playerswitch_7 (
    .key(d_latch_lock_2_7_q), .switch(bitcounter_1_1_value), .player1(playerswitch_7_player1),
    .player2(playerswitch_7_player2));
  playerswitch playerswitch_8 (
    .key(d_latch_lock_2_8_q), .switch(bitcounter_1_1_value), .player1(playerswitch_8_player1),
    .player2(playerswitch_8_player2));
  playerswitch playerswitch_9 (
    .key(d_latch_lock_2_9_q), .switch(bitcounter_1_1_value), .player1(playerswitch_9_player1),
    .player2(playerswitch_9_player2));
  or or_1 (or_1_out, and_1_out, and_2_out, and_3_out, and_4_out, and_5_out, and_6_out, and_7_out, and_8_out, and_9_out);
  bitcounter_1 bitcounter_1_1 (
    .maxvalue(1'b1), .clock(or_1_out), .reset(reset), .value(bitcounter_1_1_value));  // open: zero
  D_latch d_latch_1 (.D(playerswitch_1_player1), .Enable(xnor_1_out), .Q(p1_9));  // open: notQ
  D_latch d_latch_2 (.D(playerswitch_1_player2), .Enable(xnor_1_out), .Q(p2_9));  // open: notQ
  D_latch d_latch_3 (.D(playerswitch_2_player2), .Enable(xnor_1_out), .Q(p2_8));  // open: notQ
  D_latch d_latch_4 (.D(playerswitch_3_player2), .Enable(xnor_1_out), .Q(p2_7));  // open: notQ
  D_latch d_latch_5 (.D(playerswitch_4_player2), .Enable(xnor_1_out), .Q(p2_6));  // open: notQ
  D_latch d_latch_6 (.D(playerswitch_5_player2), .Enable(xnor_1_out), .Q(p2_5));  // open: notQ
  D_latch d_latch_7 (.D(playerswitch_6_player2), .Enable(xnor_1_out), .Q(p2_4));  // open: notQ
  D_latch d_latch_8 (.D(playerswitch_7_player2), .Enable(xnor_1_out), .Q(p2_3));  // open: notQ
  D_latch d_latch_9 (.D(playerswitch_8_player2), .Enable(xnor_1_out), .Q(p2_2));  // open: notQ
  D_latch d_latch_10 (.D(playerswitch_9_player2), .Enable(xnor_1_out), .Q(p2_1));  // open: notQ
  D_latch d_latch_11 (.D(playerswitch_2_player1), .Enable(xnor_1_out), .Q(p1_8));  // open: notQ
  D_latch d_latch_12 (.D(playerswitch_3_player1), .Enable(xnor_1_out), .Q(p1_7));  // open: notQ
  D_latch d_latch_13 (.D(playerswitch_4_player1), .Enable(xnor_1_out), .Q(p1_6));  // open: notQ
  D_latch d_latch_14 (.D(playerswitch_5_player1), .Enable(xnor_1_out), .Q(p1_5));  // open: notQ
  D_latch d_latch_15 (.D(playerswitch_6_player1), .Enable(xnor_1_out), .Q(p1_4));  // open: notQ
  D_latch d_latch_16 (.D(playerswitch_7_player1), .Enable(xnor_1_out), .Q(p1_3));  // open: notQ
  D_latch d_latch_17 (.D(playerswitch_8_player1), .Enable(xnor_1_out), .Q(p1_2));  // open: notQ
  D_latch d_latch_18 (.D(playerswitch_9_player1), .Enable(xnor_1_out), .Q(p1_1));  // open: notQ
  D_latch d_latch_19 (.D(bitcounter_1_1_value), .Enable(xnor_1_out), .Q(Astate));  // open: notQ
endmodule

module bitcounter_1 (
  input  maxvalue,
  input  clock,
  input  reset,
  output value,
  output zero
);

  Counter #(.max('h1), .width(1)) counter_1 (
    .D(maxvalue), .count(1'b1), .Q(value), .carry(zero), .up(1'b1), .clk(clock), .clr(reset));  // open: load
endmodule

module win_calc (
  input  in_1,
  input  in_2,
  input  in_3,
  input  in_4,
  input  in_5,
  input  in_6,
  input  in_7,
  input  in_8,
  input  in_9,
  output Win
);

  wire A123_out, A147_out, A159_out, A258_out, A357_out, A369_out, A456_out, A789_out;

  and A123 (A123_out, in_1, in_2, in_3);
  and A456 (A456_out, in_4, in_5, in_6);
  and A789 (A789_out, in_7, in_8, in_9);
  and A147 (A147_out, in_1, in_4, in_7);
  and A258 (A258_out, in_2, in_5, in_8);
  and A369 (A369_out, in_3, in_6, in_9);
  and A159 (A159_out, in_1, in_5, in_9);
  and A357 (A357_out, in_3, in_5, in_7);
  or or_1 (Win, A123_out, A456_out, A789_out, A147_out, A258_out, A369_out, A159_out, A357_out);
endmodule
